// Logisim project ALU_Decoder.circ as structural Verilog: 1 circuit, main circuit ALU_Decoder
module ALU_Decoder (
  input  [1:0] ALUOp_1_0,
  input  [5:0] Funct_5_0,
  output [2:0] ALUCtrl_2_0
);

  wire and_1_out, and_2_out, and_3_out, and_4_out, and_5_out, and_6_out, and_7_out, and_8_out, not_1_out,
       not_2_out, not_3_out, not_4_out, not_5_out, not_6_out, not_7_out, not_8_out, not_9_out;

  not not_1 (not_1_out, ALUOp_1_0[1]);
  not not_2 (not_2_out, ALUOp_1_0[0]);
  not not_3 (not_3_out, Funct_5_0[4]);
  not not_4 (not_4_out, Funct_5_0[2]);
  not not_5 (not_5_out, Funct_5_0[0]);
  not not_6 (not_6_out, ALUOp_1_0[1]);
  not not_7 (not_7_out, Funct_5_0[5]);
  not not_8 (not_8_out, Funct_5_0[2]);
  not not_9 (not_9_out, Funct_5_0[5]);
  and and_1 (and_1_out, not_1_out, ALUOp_1_0[0]);
  and and_2 (and_2_out, ALUOp_1_0[1], not_2_out, Funct_5_0[5], not_3_out, not_4_out, Funct_5_0[1], not_5_out);
  or or_1 (ALUCtrl_2_0[1], not_6_out, not_7_out, not_8_out, Funct_5_0[1], Funct_5_0[3], Funct_5_0[4], ALUOp_1_0[0]);
  and and_3 (and_3_out, ALUOp_1_0[1], not_9_out);
  and and_4 (and_4_out, ALUOp_1_0[1], Funct_5_0[0]);
  and and_5 (and_5_out, ALUOp_1_0[1], Funct_5_0[2], Funct_5_0[1]);
  and and_6 (and_6_out, ALUOp_1_0[1], Funct_5_0[3]);
  and and_7 (and_7_out, ALUOp_1_0[1], Funct_5_0[4]);
  and and_8 (and_8_out, ALUOp_1_0[1], ALUOp_1_0[0]);
  or or_2 (ALUCtrl_2_0[2], and_1_out, and_2_out);
  or or_3 (ALUCtrl_2_0[0], and_3_out, and_4_out, and_5_out, and_6_out, and_7_out, and_8_out);
endmodule
