// Logisim project BTB.circ as structural Verilog: 1 circuit, main circuit BTB
module BTB (
  input  [31:0] Current_PC,
  input  [31:0] Previous_PC,
  input  [31:0] TargetedAddr,
  input  EN,
  input  Branched,
  input  CLK,
  output [31:0] TargetAddr,
  output Hit
);

  wire comparator_1_eq;
  wire [30:0] ram_1_data;
  wire [31:0] bit_extender_1_out, multiplexer_1_out;
  wire [31:31] and_1_out, and_2_out;

  and and_1 (and_1_out[31], EN, Branched);
  Multiplexer #(.width(32)) multiplexer_1 (
    .in0(Current_PC), .in1(Previous_PC), .out(multiplexer_1_out), .sel(and_1_out[31]));  // open: en
  RAM #(.addrWidth(24), .dataWidth(32), .bus("separate")) ram_1 (
    .addr(multiplexer_1_out[25:2]), .din({and_1_out[31], TargetedAddr[30:0]}), .data({Hit, ram_1_data}),
    .str(and_1_out[31]), .clk(CLK), .ld(1'b1));  // open: sel, clr
  Comparator #(.width(5)) comparator_1 (
    .a(multiplexer_1_out[30:26]), .b(ram_1_data[30:26]), .eq(comparator_1_eq));  // open: gt, lt
  assign bit_extender_1_out = {{31{comparator_1_eq}}, comparator_1_eq};  // Bit_Extender bit_extender_1
  assign {and_2_out[31], TargetAddr[30:0]} = bit_extender_1_out & {Hit, ram_1_data};  // AND_Gate and_2, 32 bits wide

  assign TargetAddr[31] = 1'b0;
endmodule
