// Logisim project ControlUnit.circ as structural Verilog: 3 circuits, main circuit ControlUnit
module ControlUnit (
  input  [5:0] in_1,
  input  [5:0] in_2,
  output out_3,
  output out_4,
  output out_5,
  output out_6,
  output out_7,
  output out_8,
  output out_9,
  output [2:0] out_10
);

  wire [1:0] main_decoder_1_aluop_1_0;

  Main_Decoder main_decoder_1 (
    .Opcode_5_0(in_1), .MemtoReg(out_4), .MemWrite(out_5), .Branch(out_6), .ALUSrc(out_7), .RegDst(out_8),
    .RegWrite(out_9), .Jump(out_3), .ALUOp_1_0(main_decoder_1_aluop_1_0));
  ALU_Decoder alu_decoder_1 (.ALUOp_1_0(main_decoder_1_aluop_1_0), .Funct_5_0(in_2), .ALUCtrl_2_0(out_10));
endmodule

module ALU_Decoder (
  input  [1:0] ALUOp_1_0,
  input  [5:0] Funct_5_0,
  output [2:0] ALUCtrl_2_0
);

  wire and_1_out, and_2_out, and_3_out, and_4_out, and_5_out, and_6_out, and_7_out, and_8_out, not_1_out,
       not_2_out, not_3_out, not_4_out, not_5_out, not_6_out, not_7_out, not_8_out, not_9_out;

  not not_1 (not_1_out, ALUOp_1_0[1]);
  not not_2 (not_2_out, ALUOp_1_0[0]);
  not not_3 (not_3_out, Funct_5_0[4]);
  not not_4 (not_4_out, Funct_5_0[2]);
  not not_5 (not_5_out, Funct_5_0[0]);
  not not_6 (not_6_out, ALUOp_1_0[1]);
  not not_7 (not_7_out, Funct_5_0[5]);
  not not_8 (not_8_out, Funct_5_0[2]);
  not not_9 (not_9_out, Funct_5_0[5]);
  and and_1 (and_1_out, not_1_out, ALUOp_1_0[0]);
  and and_2 (and_2_out, ALUOp_1_0[1], not_2_out, Funct_5_0[5], not_3_out, not_4_out, Funct_5_0[1], not_5_out);
  or or_1 (ALUCtrl_2_0[1], not_6_out, not_7_out, not_8_out, Funct_5_0[1], Funct_5_0[3], Funct_5_0[4], ALUOp_1_0[0]);
  and and_3 (and_3_out, ALUOp_1_0[1], not_9_out);
  and and_4 (and_4_out, ALUOp_1_0[1], Funct_5_0[0]);
  and and_5 (and_5_out, ALUOp_1_0[1], Funct_5_0[2], Funct_5_0[1]);
  and and_6 (and_6_out, ALUOp_1_0[1], Funct_5_0[3]);
  and and_7 (and_7_out, ALUOp_1_0[1], Funct_5_0[4]);
  and and_8 (and_8_out, ALUOp_1_0[1], ALUOp_1_0[0]);
  or or_2 (ALUCtrl_2_0[2], and_1_out, and_2_out);
  or or_3 (ALUCtrl_2_0[0], and_3_out, and_4_out, and_5_out, and_6_out, and_7_out, and_8_out);
endmodule

module Main_Decoder (
  input  [5:0] Opcode_5_0,
  output MemtoReg,
  output MemWrite,
  output Branch,
  output ALUSrc,
  output RegDst,
  output RegWrite,
  output Jump,
  output [1:0] ALUOp_1_0
);

  wire and_4_out, and_5_out, and_7_out, and_8_out, not_1_out, not_2_out, not_3_out, not_4_out, not_5_out,
       not_6_out, not_7_out, not_8_out, not_9_out, not_10_out, not_11_out, not_12_out, not_13_out,
       not_14_out, not_15_out, not_16_out, not_17_out, not_18_out, not_19_out, not_20_out, not_21_out,
       not_22_out, not_23_out, not_24_out, not_25_out, not_26_out, not_27_out, not_28_out, not_29_out,
       not_30_out, not_31_out, not_32_out, not_33_out, not_34_out, not_35_out, not_36_out, not_37_out,
       not_38_out, not_39_out, not_40_out, not_41_out, not_42_out, not_43_out, not_44_out;

  not not_1 (not_1_out, Opcode_5_0[4]);
  not not_2 (not_2_out, Opcode_5_0[2]);
  not not_3 (not_3_out, Opcode_5_0[4]);
  not not_4 (not_4_out, Opcode_5_0[2]);
  not not_5 (not_5_out, Opcode_5_0[5]);
  not not_6 (not_6_out, Opcode_5_0[4]);
  not not_7 (not_7_out, Opcode_5_0[3]);
  not not_8 (not_8_out, Opcode_5_0[1]);
  not not_9 (not_9_out, Opcode_5_0[0]);
  not not_10 (not_10_out, Opcode_5_0[5]);
  not not_11 (not_11_out, Opcode_5_0[4]);
  not not_12 (not_12_out, Opcode_5_0[2]);
  not not_13 (not_13_out, Opcode_5_0[1]);
  not not_14 (not_14_out, Opcode_5_0[0]);
  not not_15 (not_15_out, Opcode_5_0[4]);
  not not_16 (not_16_out, Opcode_5_0[2]);
  not not_17 (not_17_out, Opcode_5_0[5]);
  not not_18 (not_18_out, Opcode_5_0[4]);
  not not_19 (not_19_out, Opcode_5_0[3]);
  not not_20 (not_20_out, Opcode_5_0[2]);
  not not_21 (not_21_out, Opcode_5_0[0]);
  not not_22 (not_22_out, Opcode_5_0[5]);
  not not_23 (not_23_out, Opcode_5_0[4]);
  not not_24 (not_24_out, Opcode_5_0[2]);
  not not_25 (not_25_out, Opcode_5_0[1]);
  not not_26 (not_26_out, Opcode_5_0[0]);
  not not_27 (not_27_out, Opcode_5_0[4]);
  not not_28 (not_28_out, Opcode_5_0[3]);
  not not_29 (not_29_out, Opcode_5_0[2]);
  not not_30 (not_30_out, Opcode_5_0[5]);
  not not_31 (not_31_out, Opcode_5_0[4]);
  not not_32 (not_32_out, Opcode_5_0[3]);
  not not_33 (not_33_out, Opcode_5_0[2]);
  not not_34 (not_34_out, Opcode_5_0[0]);
  not not_35 (not_35_out, Opcode_5_0[5]);
  not not_36 (not_36_out, Opcode_5_0[4]);
  not not_37 (not_37_out, Opcode_5_0[3]);
  not not_38 (not_38_out, Opcode_5_0[2]);
  not not_39 (not_39_out, Opcode_5_0[0]);
  not not_40 (not_40_out, Opcode_5_0[5]);
  not not_41 (not_41_out, Opcode_5_0[4]);
  not not_42 (not_42_out, Opcode_5_0[3]);
  not not_43 (not_43_out, Opcode_5_0[1]);
  not not_44 (not_44_out, Opcode_5_0[0]);
  and and_1 (MemtoReg, Opcode_5_0[5], not_1_out, not_2_out, Opcode_5_0[1], Opcode_5_0[0]);
  and and_2 (MemWrite, Opcode_5_0[5], not_3_out, Opcode_5_0[3], not_4_out, Opcode_5_0[1], Opcode_5_0[0]);
  and and_3 (Branch, not_5_out, not_6_out, not_7_out, Opcode_5_0[2], not_8_out, not_9_out);
  and and_4 (and_4_out, not_10_out, not_11_out, Opcode_5_0[3], not_12_out, not_13_out, not_14_out);
  and and_5 (and_5_out, Opcode_5_0[5], not_15_out, not_16_out, Opcode_5_0[1], Opcode_5_0[0]);
  and and_6 (RegDst, not_17_out, not_18_out, not_19_out, not_20_out, not_21_out);
  and and_7 (and_7_out, not_22_out, not_23_out, not_24_out, not_25_out, not_26_out);
  and and_8 (and_8_out, Opcode_5_0[5], not_27_out, not_28_out, not_29_out, Opcode_5_0[1], Opcode_5_0[0]);
  and and_9 (Jump, not_30_out, not_31_out, not_32_out, not_33_out, Opcode_5_0[1], not_34_out);
  and and_10 (ALUOp_1_0[1], not_35_out, not_36_out, not_37_out, not_38_out, not_39_out);
  and and_11 (ALUOp_1_0[0], not_40_out, not_41_out, not_42_out, Opcode_5_0[2], not_43_out, not_44_out);
  or or_1 (ALUSrc, and_4_out, and_5_out);
  or or_2 (RegWrite, and_7_out, and_8_out);
endmodule
