// Logisim project Hazard_Detect.circ as structural Verilog: 1 circuit, main circuit Hazard_Detect
module Hazard_Detect (
  input  ID_EX_MemtoReg,
  input  [4:0] IF_ID_RegRs,
  input  [4:0] ID_EX_RegRt,
  input  [4:0] IF_ID_RegRt,
  output PC_En,
  output IF_ID_RegEn,
  output FlushEn
);

  wire comparator_1_eq, comparator_2_eq, or_1_out;

  Comparator #(.width(5)) comparator_1 (.a(IF_ID_RegRs), .b(ID_EX_RegRt), .eq(comparator_1_eq));  // open: gt, lt
  Comparator #(.width(5)) comparator_2 (.a(ID_EX_RegRt), .b(IF_ID_RegRt), .eq(comparator_2_eq));  // open: gt, lt
  or or_1 (or_1_out, comparator_1_eq, comparator_2_eq);
  and and_1 (FlushEn, ID_EX_MemtoReg, or_1_out);
  not not_1 (PC_En, FlushEn);
  not not_2 (IF_ID_RegEn, FlushEn);
endmodule
