// Logisim project Hazard_Forwarding.circ as structural Verilog: 2 circuits, main circuit Data_Hazard_Forwarding
module Data_Hazard_Forwarding (
  input  RegWriteM,
  input  [4:0] EX_MEM_RegRd,
  input  [4:0] ID_EX_RegRs,
  input  [4:0] ID_EX_RegRt,
  input  [4:0] MEM_WB_RegRd,
  input  RegWriteW,
  output [1:0] MUX_A,
  output [1:0] MUX_B
);

  wire comparator_1_eq, comparator_2_eq, comparator_3_eq, comparator_4_eq, comparator_5_eq, comparator_6_eq,
       not_1_out, not_2_out;

  Comparator #(.width(5)) comparator_1 (.a(ID_EX_RegRs), .b(EX_MEM_RegRd), .eq(comparator_1_eq));  // open: gt, lt
  Comparator #(.width(5)) comparator_2 (.a(EX_MEM_RegRd), .b({5{1'b0}}), .eq(comparator_2_eq));  // open: gt, lt
  not not_1 (not_1_out, comparator_2_eq);
  Comparator #(.width(5)) comparator_3 (.a(EX_MEM_RegRd), .b(ID_EX_RegRt), .eq(comparator_3_eq));  // open: gt, lt
  Comparator #(.width(5)) comparator_4 (.a(ID_EX_RegRs), .b(MEM_WB_RegRd), .eq(comparator_4_eq));  // open: gt, lt
  not not_2 (not_2_out, comparator_5_eq);
  Comparator #(.width(5)) comparator_5 (.a({5{1'b0}}), .b(MEM_WB_RegRd), .eq(comparator_5_eq));  // open: gt, lt
  Comparator #(.width(5)) comparator_6 (.a(MEM_WB_RegRd), .b(ID_EX_RegRt), .eq(comparator_6_eq));  // open: gt, lt
  and and_1 (MUX_A[0], RegWriteM, comparator_1_eq, not_1_out);
  and and_2 (MUX_B[0], not_1_out, comparator_3_eq, RegWriteM);
  and and_3 (MUX_A[1], ~MUX_A[0], comparator_4_eq, not_2_out, RegWriteW);  // AND_Gate
  and and_4 (MUX_B[1], ~MUX_B[0], not_2_out, comparator_6_eq, RegWriteW);  // AND_Gate

  // Notes on the sheet:
  //   RegWriteW: pull=up
  //   No Hazard X -> MUX : 00
  //   EX_Hazard -> MUX : 01
  //   MEM_Hazard -> MUX : 10
  //   ForwardA = 01 (EX)
  //   ForwardB = 01(EX)
  //   ForwardA = 10(MEM)
  //   ForwardB = 10(MEM)
endmodule

module Ctrl_Hazard_Forwarding (
  input  [4:0] RsD,
  input  [4:0] RdM,
  input  RegWriteM,
  input  [4:0] RtD,
  output ForwardAD,
  output ForwardBD
);

  wire comparator_1_eq, comparator_2_eq, comparator_3_eq, comparator_4_eq;

  Comparator #(.width(5)) comparator_1 (.a(RsD), .b({5{1'b0}}), .eq(comparator_1_eq));  // open: gt, lt
  Comparator #(.width(5)) comparator_2 (.a(RsD), .b(RdM), .eq(comparator_2_eq));  // open: gt, lt
  Comparator #(.width(5)) comparator_3 (.a(RdM), .b(RtD), .eq(comparator_3_eq));  // open: gt, lt
  Comparator #(.width(5)) comparator_4 (.a({5{1'b0}}), .b(RtD), .eq(comparator_4_eq));  // open: gt, lt
  and and_1 (ForwardAD, ~comparator_1_eq, comparator_2_eq, RegWriteM);  // AND_Gate
  and and_2 (ForwardBD, RegWriteM, comparator_3_eq, ~comparator_4_eq);  // AND_Gate
endmodule
