// Logisim project Hazard_Unit.circ as structural Verilog: 1 circuit, main circuit Hazard_Unit
module Hazard_Unit (
  input  CLK,
  input  BranchD,
  input  RegWriteE,
  input  RegWriteM,
  input  RegWriteW,
  input  MemtoRegM,
  input  MemtoRegE,
  input  [4:0] WriteRegE,
  input  [4:0] RsD,
  input  [4:0] RsE,
  input  [4:0] RtD,
  input  [4:0] RtE,
  input  [4:0] WriteRegM,
  input  [4:0] WriteRegW,
  output StallF,
  output StallD,
  output FlushE,
  output [1:0] ForwardAE,
  output [1:0] ForwardBE,
  output ForwardAD,
  output ForwardBD
);

  wire ctrl_hazard_stall_1_branchstall, d_ff_1_q, data_hazard_stall_1_lwstall;
  wire [4:0] WriteRegM_t;

  Data_Hazard_Stall data_hazard_stall_1 (
    .MemtoRegE(MemtoRegE), .rsD(RsD), .rtE(RtE), .rtD(RtD), .lwstall(data_hazard_stall_1_lwstall));
  Ctrl_Hazard_Stall ctrl_hazard_stall_1 (
    .RegWriteE(RegWriteE), .rsD(RsD), .WriteRegE(WriteRegE), .rtD(RtD), .BranchD(BranchD),
    .WriteRegM(WriteRegM_t), .MemtoRegM(MemtoRegM), .BranchStall(ctrl_hazard_stall_1_branchstall));
  Data_Hazard_Forwarding data_hazard_forwarding_1 (
    .RegWriteM(RegWriteM), .RegWriteW(RegWriteW), .ID_EX_RegRs(RsE), .EX_MEM_RegRd(WriteRegM),
    .MUX_A(ForwardAE), .ID_EX_RegRt(RtE), .MUX_B(ForwardBE), .MEM_WB_RegRd(WriteRegW));
  Ctrl_Hazard_Forwarding ctrl_hazard_forwarding_1 (
    .RsD(RsD), .RdM(WriteRegM), .RegWriteM(RegWriteM), .RtD(RtD), .ForwardAD(ForwardAD), .ForwardBD(ForwardBD));
  or or_1 (StallD, data_hazard_stall_1_lwstall, ctrl_hazard_stall_1_branchstall);
  D_Flip_Flop #(.trigger("falling")) d_ff_1 (.clk(CLK), .D(StallD), .Q(d_ff_1_q));  // open: Qn, preset, en, reset
  and and_1 (FlushE, CLK, d_ff_1_q);

  assign StallF = StallD;

  // Other names for the same wires on the sheet: RdM[4:0] = WriteRegM; RdW[4:0] = WriteRegW

  // Notes on the sheet:
  //   ForwardAE: pull=up
  //   ForwardBE: pull=up
endmodule
