// Logisim project MIPS.circ as structural Verilog: 2 circuits, main circuit main
module main (
);

  wire and_1_out, and_2_out, and_3_out, and_4_out, bht_1_out_4, btb_1_hit, buff_20_1_out_2, buff_20_2_out_2,
       buff_20_3_out_2, CLK, comparator_1_eq, controlunit_1_out_3, controlunit_1_out_4, controlunit_1_out_5,
       controlunit_1_out_6, controlunit_1_out_7, controlunit_1_out_8, controlunit_1_out_9,
       hazard_unit_1_flushe, hazard_unit_1_forwardad, hazard_unit_1_forwardbd, hazard_unit_1_forwardm,
       hazard_unit_1_stalld, hazard_unit_1_stallf, or_1_out, or_2_out, or_3_out, reg_stage2_1_alusrce,
       reg_stage2_1_memtorege, reg_stage2_1_memwritee, reg_stage2_1_regdste, reg_stage2_1_regwritee,
       reg_stage3_1_memtoregm, reg_stage3_1_memwritem, reg_stage3_1_regwritem, reg_stage4_1_memtoregw,
       reg_stage4_1_regwritew;
  wire [1:0] hazard_unit_1_forwardae, hazard_unit_1_forwardbe;
  wire [3:0] adder_1_out_2, controlunit_1_out_10, reg_stage2_1_aluctrle;
  wire [4:0] multiplexer_7_out, reg_stage2_1_rde, reg_stage2_1_rse, reg_stage2_1_rte, reg_stage3_1_writeregm,
       reg_stage4_1_writeregw;
  wire [27:0] adder_1_out, bit_extender_1_out, shifter_1_out;
  wire [31:0] adder_2_out, alu_1_alu_result, bit_extender_2_out, btb_1_targetaddr, datamem_1_rd,
       instmem_1_out_2, multiplexer_1_out, multiplexer_2_out, multiplexer_3_out, multiplexer_4_out,
       multiplexer_5_out, multiplexer_6_out, multiplexer_8_out, multiplexer_9_out, multiplexer_10_out,
       multiplexer_11_out, multiplexer_12_out, PC_q, reg_stage1_1_instrd, reg_stage1_1_pc_2,
       reg_stage1_1_pcplus4d, reg_stage2_1_signimme, reg_stage2_1_srcae, reg_stage2_1_srcbe,
       reg_stage3_1_aluoutm, reg_stage3_1_writedatam, reg_stage4_1_aluoutw, reg_stage4_1_readdataw,
       regfile32_1_rd1, regfile32_1_rd2, shifter_2_out;

  Clock clock_1 (.out(CLK));
  Multiplexer #(.width(32)) multiplexer_1 (
    .in0({adder_1_out_2, adder_1_out}), .in1(adder_2_out), .out(multiplexer_1_out), .sel(and_4_out));  // open: en
  Multiplexer #(.width(32)) multiplexer_2 (
    .in0(multiplexer_1_out), .in1({adder_1_out_2, shifter_1_out}), .out(multiplexer_2_out),
    .sel(controlunit_1_out_3));  // open: en
  Register #(.width(32)) PC (.D(multiplexer_2_out), .en(hazard_unit_1_stallf), .Q(PC_q), .clk(CLK));  // open: clr
  Multiplexer #(.width(32)) multiplexer_3 (
    .in0(adder_2_out), .in1({adder_1_out_2, shifter_1_out}), .out(multiplexer_3_out),
    .sel(controlunit_1_out_3));  // open: en
  Adder #(.width(32)) adder_1 (.a(PC_q), .b(32'h4), .out({adder_1_out_2, adder_1_out}));  // open: cin, cout
  or or_1 (or_1_out, and_4_out, controlunit_1_out_3);
  BTB btb_1 (
    .Current_PC(PC_q), .TargetedAddr(multiplexer_3_out), .Branched(or_1_out), .CLK(CLK),
    .TargetAddr(btb_1_targetaddr), .Hit(btb_1_hit), .Previous_PC(reg_stage1_1_pc_2), .EN(hazard_unit_1_stallf));
  Buff_20 buff_20_1 (.in_1(CLK), .out_2(buff_20_1_out_2));
  Buff_20 buff_20_2 (.in_1(buff_20_1_out_2), .out_2(buff_20_2_out_2));
  BHT bht_1 (.A(or_1_out), .Branch(or_2_out), .CLK(buff_20_2_out_2), .out_4(bht_1_out_4));
  Hazard_Unit hazard_unit_1 (
    .BranchD(controlunit_1_out_6), .RegWriteE(reg_stage2_1_regwritee), .RegWriteM(reg_stage3_1_memwritem),
    .RegWriteW(reg_stage4_1_regwritew), .MemtoRegM(reg_stage3_1_regwritem),
    .MemtoRegE(reg_stage2_1_memtorege), .WriteRegE(multiplexer_7_out), .RsD(reg_stage1_1_instrd[25:21]),
    .RsE(reg_stage2_1_rse), .RtD(reg_stage1_1_instrd[20:16]), .RtE(reg_stage2_1_rte),
    .WriteRegM(reg_stage3_1_writeregm), .WriteRegW(reg_stage4_1_writeregw), .StallF(hazard_unit_1_stallf),
    .StallD(hazard_unit_1_stalld), .FlushE(hazard_unit_1_flushe), .ForwardAE(hazard_unit_1_forwardae),
    .ForwardBE(hazard_unit_1_forwardbe), .ForwardAD(hazard_unit_1_forwardad),
    .ForwardBD(hazard_unit_1_forwardbd), .CLK(CLK), .ForwardM(hazard_unit_1_forwardm),
    .MemWriteD(controlunit_1_out_5), .MemWriteE(reg_stage2_1_memtorege));
  and and_1 (and_1_out, hazard_unit_1_stallf, controlunit_1_out_6);
  or or_2 (or_2_out, controlunit_1_out_3, and_1_out);
  and and_2 (and_2_out, bht_1_out_4, btb_1_hit);
  Multiplexer #(.width(32)) multiplexer_4 (
    .in0(PC_q), .in1(btb_1_targetaddr), .out(multiplexer_4_out), .sel(and_2_out));  // open: en
  Reg_Stage1 reg_stage1_1 (
    .CLR(and_3_out), .EN(hazard_unit_1_stalld), .CLK(CLK), .InstrF(instmem_1_out_2),
    .PCPlus4F({adder_1_out_2, adder_1_out}), .InstrD(reg_stage1_1_instrd), .PCPlus4D(reg_stage1_1_pcplus4d),
    .PC(PC_q), .PC_2(reg_stage1_1_pc_2));
  InstMem instmem_1 (.A(multiplexer_4_out), .out_2(instmem_1_out_2));
  or or_3 (or_3_out, and_4_out, controlunit_1_out_3);
  and and_3 (and_3_out, or_3_out, ~and_2_out);  // AND_Gate
  assign bit_extender_1_out = {{2{reg_stage1_1_instrd[25]}}, reg_stage1_1_instrd[25:0]};  // Bit_Extender bit_extender_1
  ControlUnit controlunit_1 (
    .out_3(controlunit_1_out_3), .in_1(reg_stage1_1_instrd[31:26]), .in_2(reg_stage1_1_instrd[5:0]),
    .out_4(controlunit_1_out_4), .out_5(controlunit_1_out_5), .out_6(controlunit_1_out_6),
    .out_7(controlunit_1_out_7), .out_8(controlunit_1_out_8), .out_9(controlunit_1_out_9),
    .out_10(controlunit_1_out_10));
  assign bit_extender_2_out = {{16{reg_stage1_1_instrd[15]}}, reg_stage1_1_instrd[15:0]};  // Bit_Extender bit_extender_2
  Shifter #(.width(28)) shifter_1 (.in(bit_extender_1_out), .\dist (5'b00010), .out(shifter_1_out));
  Buff_20 buff_20_3 (.in_1(CLK), .out_2(buff_20_3_out_2));
  RegFile32 regfile32_1 (
    .AD1(reg_stage1_1_instrd[25:21]), .AD2(reg_stage1_1_instrd[20:16]), .CLK(buff_20_3_out_2),
    .WE(reg_stage4_1_regwritew), .AD3(reg_stage4_1_writeregw), .WD3(multiplexer_12_out),
    .RD1(regfile32_1_rd1), .RD2(regfile32_1_rd2));
  Comparator #(.width(32)) comparator_1 (
    .a(multiplexer_5_out), .b(multiplexer_6_out), .eq(comparator_1_eq));  // open: gt, lt
  Shifter #(.width(32)) shifter_2 (.in(bit_extender_2_out), .\dist (5'b00010), .out(shifter_2_out));
  and and_4 (and_4_out, comparator_1_eq, controlunit_1_out_6);
  Multiplexer #(.width(32)) multiplexer_5 (
    .in0(regfile32_1_rd1), .in1(reg_stage3_1_aluoutm), .out(multiplexer_5_out), .sel(hazard_unit_1_forwardad));  // open: en
  Adder #(.width(32)) adder_2 (.a(shifter_2_out), .b(reg_stage1_1_pcplus4d), .out(adder_2_out));  // open: cin, cout
  Multiplexer #(.width(32)) multiplexer_6 (
    .in0(regfile32_1_rd2), .in1(reg_stage3_1_aluoutm), .out(multiplexer_6_out), .sel(hazard_unit_1_forwardbd));  // open: en
  Reg_Stage2 reg_stage2_1 (
    .CLK(CLK), .CLR(hazard_unit_1_flushe), .MemtoRegD(controlunit_1_out_4), .MemWriteD(controlunit_1_out_5),
    .ALUSrcD(controlunit_1_out_7), .RegDstD(controlunit_1_out_8), .RegWriteD(controlunit_1_out_9),
    .ALUCtrlD(controlunit_1_out_10), .SrcAD(regfile32_1_rd1), .SrcBD(regfile32_1_rd2),
    .RsD(reg_stage1_1_instrd[25:21]), .RtD(reg_stage1_1_instrd[20:16]), .RdD(reg_stage1_1_instrd[15:11]),
    .SignImmD(bit_extender_2_out), .MemtoRegE(reg_stage2_1_memtorege), .MemWriteE(reg_stage2_1_memwritee),
    .ALUSrcE(reg_stage2_1_alusrce), .RegDstE(reg_stage2_1_regdste), .RegWriteE(reg_stage2_1_regwritee),
    .ALUCtrlE(reg_stage2_1_aluctrle), .SrcAE(reg_stage2_1_srcae), .SrcBE(reg_stage2_1_srcbe),
    .RsE(reg_stage2_1_rse), .RtE(reg_stage2_1_rte), .RdE(reg_stage2_1_rde), .SignImmE(reg_stage2_1_signimme));
  Multiplexer #(.width(5)) multiplexer_7 (
    .in0(reg_stage2_1_rte), .in1(reg_stage2_1_rde), .out(multiplexer_7_out), .sel(reg_stage2_1_regdste));  // open: en
  Multiplexer #(.select(2), .width(32)) multiplexer_8 (
    .in0(reg_stage2_1_srcbe), .in1(reg_stage3_1_aluoutm), .in2(multiplexer_12_out), .out(multiplexer_8_out),
    .sel(hazard_unit_1_forwardbe));  // open: in3, en
  Multiplexer #(.select(2), .width(32)) multiplexer_9 (
    .in0(reg_stage2_1_srcae), .in1(reg_stage3_1_aluoutm), .in2(multiplexer_12_out), .out(multiplexer_9_out),
    .sel(hazard_unit_1_forwardae));  // open: in3, en
  Multiplexer #(.width(32)) multiplexer_10 (
    .in0(multiplexer_8_out), .in1(reg_stage2_1_signimme), .out(multiplexer_10_out), .sel(reg_stage2_1_alusrce));  // open: en
  Reg_Stage3 reg_stage3_1 (
    .RegWriteE(reg_stage2_1_memtorege), .MemtoRegE(reg_stage2_1_memwritee),
    .MemWriteE(reg_stage2_1_regwritee), .ALUOutE(alu_1_alu_result), .WriteDataE(multiplexer_8_out),
    .WriteRegE(multiplexer_7_out), .RegWriteM(reg_stage3_1_regwritem), .MemtoRegM(reg_stage3_1_memtoregm),
    .MemWriteM(reg_stage3_1_memwritem), .ALUOutM(reg_stage3_1_aluoutm), .WriteDataM(reg_stage3_1_writedatam),
    .WriteRegM(reg_stage3_1_writeregm), .CLK(CLK));
  ALU alu_1 (
    .SrcA(multiplexer_9_out), .SrcB(multiplexer_10_out), .ALU_Control(reg_stage2_1_aluctrle),
    .ALU_Result(alu_1_alu_result));  // open: Zero
  Multiplexer #(.width(32)) multiplexer_11 (
    .in0(reg_stage3_1_writedatam), .in1(multiplexer_12_out), .out(multiplexer_11_out),
    .sel(hazard_unit_1_forwardm));  // open: en
  Reg_Stage4 reg_stage4_1 (
    .CLK(CLK), .RegWriteM(reg_stage3_1_memwritem), .MemtoRegM(reg_stage3_1_regwritem),
    .ALUOutM(reg_stage3_1_aluoutm), .ReadDataM(datamem_1_rd), .WriteRegM(reg_stage3_1_writeregm),
    .RegWriteW(reg_stage4_1_regwritew), .MemtoRegW(reg_stage4_1_memtoregw), .ALUOutW(reg_stage4_1_aluoutw),
    .ReadDataW(reg_stage4_1_readdataw), .WriteRegW(reg_stage4_1_writeregw));
  DataMem datamem_1 (
    .CLK(CLK), .WE(reg_stage3_1_memtoregm), .WD(multiplexer_11_out), .A(reg_stage3_1_aluoutm),
    .RD(datamem_1_rd));
  Multiplexer #(.width(32)) multiplexer_12 (
    .in0(reg_stage4_1_aluoutw), .in1(reg_stage4_1_readdataw), .out(multiplexer_12_out),
    .sel(reg_stage4_1_memtoregw));  // open: en
endmodule

module Buff_20 (
  input  in_1,
  output out_2
);

  wire buffer_1_out, buffer_2_out, buffer_3_out, buffer_4_out, buffer_5_out, buffer_6_out, buffer_7_out,
       buffer_8_out, buffer_9_out, buffer_10_out, buffer_11_out, buffer_12_out, buffer_13_out, buffer_14_out,
       buffer_15_out, buffer_16_out, buffer_17_out, buffer_18_out, buffer_20_out;

  buf buffer_1 (buffer_1_out, buffer_2_out);
  buf buffer_2 (buffer_2_out, in_1);
  buf buffer_3 (buffer_3_out, buffer_4_out);
  buf buffer_4 (buffer_4_out, buffer_5_out);
  buf buffer_5 (buffer_5_out, buffer_1_out);
  buf buffer_6 (buffer_6_out, buffer_3_out);
  buf buffer_7 (buffer_7_out, buffer_8_out);
  buf buffer_8 (buffer_8_out, buffer_10_out);
  buf buffer_9 (buffer_9_out, buffer_7_out);
  buf buffer_10 (buffer_10_out, buffer_6_out);
  buf buffer_11 (buffer_11_out, buffer_13_out);
  buf buffer_12 (buffer_12_out, buffer_11_out);
  buf buffer_13 (buffer_13_out, buffer_14_out);
  buf buffer_14 (buffer_14_out, buffer_9_out);
  buf buffer_15 (buffer_15_out, buffer_12_out);
  buf buffer_16 (buffer_16_out, buffer_18_out);
  buf buffer_17 (buffer_17_out, buffer_15_out);
  buf buffer_18 (buffer_18_out, buffer_17_out);
  buf buffer_19 (out_2, buffer_20_out);
  buf buffer_20 (buffer_20_out, buffer_16_out);
endmodule
