// Logisim project Main_Decoder.circ as structural Verilog: 1 circuit, main circuit Main_Decoder
module Main_Decoder (
  input  [5:0] in_1,
  output MemtoReg,
  output MemWrite,
  output Brach,
  output ALUSrc,
  output RegDst,
  output RegWrite,
  output Jump,
  output [1:0] ALUOp_1_0
);

  wire not_2_out, not_3_out, not_4_out, not_5_out, not_6_out, not_7_out;

  and and_1 (MemWrite, in_1[5], in_1[3]);
  or or_1 (ALUSrc, in_1[1], in_1[3]);
  not not_1 (RegDst, in_1[3]);
  not not_2 (not_2_out, in_1[2]);
  not not_3 (not_3_out, in_1[1]);
  not not_4 (not_4_out, in_1[0]);
  not not_5 (not_5_out, in_1[3]);
  not not_6 (not_6_out, in_1[2]);
  not not_7 (not_7_out, in_1[1]);
  and and_2 (RegWrite, not_2_out, not_3_out);
  and and_3 (Jump, in_1[1], not_4_out);
  and and_4 (ALUOp_1_0[1], not_5_out, not_6_out, not_7_out);

  assign ALUOp_1_0[0] = in_1[2];
  assign Brach = in_1[2];
  assign MemtoReg = in_1[1];
endmodule
